// Logisim project cronometro.circ as structural Verilog: 4 circuits, main circuit main
module main (
);

  wire clock_1_out, stop6_1_output, stop6_2_output, stop10_1_output, stop10_2_output;
  wire [3:0] count4bit_1_out_3, count4bit_2_out_3, count4bit_3_out_3, count4bit_4_out_3;

  Clock clock_1 (.out(clock_1_out));
  count4Bit count4bit_1 (.Input(clock_1_out), .Clear(stop10_1_output), .out_3(count4bit_1_out_3));
  stop10 stop10_1 (.Input(count4bit_1_out_3), .Output(stop10_1_output));
  count4Bit count4bit_2 (.Input(stop10_1_output), .Clear(stop6_1_output), .out_3(count4bit_2_out_3));
  stop6 stop6_1 (.Input(count4bit_2_out_3), .Output(stop6_1_output));
  count4Bit count4bit_3 (.Input(stop6_1_output), .Clear(stop10_2_output), .out_3(count4bit_3_out_3));
  stop10 stop10_2 (.Input(count4bit_3_out_3), .Output(stop10_2_output));
  Hex_Digit_Display hex_digit_display_1 (.value(count4bit_4_out_3));  // open: dp
  Hex_Digit_Display hex_digit_display_2 (.value(count4bit_3_out_3));  // open: dp
  count4Bit count4bit_4 (.Input(stop10_2_output), .Clear(stop6_2_output), .out_3(count4bit_4_out_3));
  Hex_Digit_Display hex_digit_display_3 (.value(count4bit_2_out_3));  // open: dp
  stop6 stop6_2 (.Input(count4bit_4_out_3), .Output(stop6_2_output));
  Hex_Digit_Display hex_digit_display_4 (.value(count4bit_1_out_3));  // open: dp

  // Notes on the sheet:
  //   Cronometro
  //   clock = 2hz
endmodule

module stop10 (
  input  [3:0] Input,
  output Output
);

  wire not_1_out, not_2_out;

  not not_1 (not_1_out, Input[0]);
  not not_2 (not_2_out, Input[2]);
  and and_1 (Output, not_1_out, Input[1], not_2_out, Input[3]);
endmodule

module stop6 (
  input  [3:0] Input,
  output Output
);

  wire not_1_out, not_2_out;

  not not_1 (not_1_out, Input[0]);
  not not_2 (not_2_out, Input[3]);
  and and_1 (Output, not_1_out, Input[1], Input[2], not_2_out);
endmodule

module count4Bit (
  input  Input,
  input  Clear,
  output [3:0] out_3
);

  wire j_k_ff_1_qn, j_k_ff_2_qn, j_k_ff_3_qn;

  J_K_Flip_Flop j_k_ff_1 (
    .J(1'b1), .clk(Input), .K(1'b1), .Q(out_3[0]), .Qn(j_k_ff_1_qn), .reset(Clear));  // open: preset, en
  J_K_Flip_Flop j_k_ff_2 (
    .J(1'b1), .clk(j_k_ff_1_qn), .K(1'b1), .Q(out_3[1]), .Qn(j_k_ff_2_qn), .reset(Clear));  // open: preset, en
  J_K_Flip_Flop j_k_ff_3 (
    .J(1'b1), .clk(j_k_ff_2_qn), .K(1'b1), .Q(out_3[2]), .Qn(j_k_ff_3_qn), .reset(Clear));  // open: preset, en
  J_K_Flip_Flop j_k_ff_4 (.J(1'b1), .clk(j_k_ff_3_qn), .K(1'b1), .Q(out_3[3]), .reset(Clear));  // open: Qn, preset, en
endmodule
