// Logisim project open-the-caveau.circ as structural Verilog: 7 circuits, main circuit main
module main (
  input  in_1
);

  wire _0, _1, _2, _3, _4, _5, _6, _7, _8, _9, _1944, _1945, _1946, _1947, AL_AHLY, BOCA_JUNIORS,
       clock_1_out, Falso, Falso2, j_k_ff_1_qn, MILAN, N1, N2, N3, N4, nor_1_out, or_1_out, or_2_out,
       or_3_out, or_4_out, or_5_out, or_6_out, or_7_out, priority_encoder_1_gs, priority_encoder_1_out,
       priority_encoder_2_gs, priority_encoder_2_out, priority_encoder_3_gs, priority_encoder_4_gs,
       priority_encoder_4_out, priority_encoder_5_gs, priority_encoder_5_out, REAL_MADRID, ResetPin, ris1,
       ris2, ris3, ris4, Start, status, stop6_1_output, stop6_2_output, stop10_1_output, stop10_2_output,
       Vero, Vero2;
  wire [3:0] cifra1, cifra1Ins, cifra2, cifra2Ins, cifra3, cifra3Ins, cifra4, cifra4Ins, cifraS1, cifraS2,
       cifraS3, cifraS4, min1, min2, priority_encoder_3_out, sec1, sec2;
  wire [18:0] statuscaveau_1_out_2, statuscaveau_1_out_3, statuscaveau_1_out_4, statuscaveau_1_out_5,
       statuscaveau_1_out_6, statuscaveau_1_out_7, statuscaveau_1_out_8, statuscaveau_1_out_9,
       statuscaveau_1_out_10, statuscaveau_1_out_11, statuscaveau_1_out_12, statuscaveau_1_out_13,
       statuscaveau_1_out_14, statuscaveau_1_out_15, statuscaveau_1_out_16, statuscaveau_1_out_17,
       statuscaveau_1_out_18, statuscaveau_1_out_19, statuscaveau_1_out_20, statuscaveau_1_out_21;
  wire [31:0] missioncomplete_1_out_2, missioncomplete_1_out_3, missioncomplete_1_out_4,
       missioncomplete_1_out_5, missioncomplete_1_out_6, missioncomplete_1_out_7, missioncomplete_1_out_8,
       missioncomplete_1_out_9, missioncomplete_1_out_10, missioncomplete_1_out_11, missioncomplete_1_out_12,
       missioncomplete_1_out_13, missioncomplete_1_out_14, missioncomplete_1_out_15, missioncomplete_1_out_16;

  Button button_1 (.out(_1945));
  Button button_2 (.out(_1947));
  Button button_3 (.out(Vero));
  Button button_4 (.out(AL_AHLY));
  Button button_5 (.out(MILAN));
  Button button_6 (.out(Vero2));
  Hex_Digit_Display hex_digit_display_1 (.value(cifraS1));  // open: dp
  LED led_1 (.in(N1));
  Hex_Digit_Display hex_digit_display_2 (.value(cifra1Ins));  // open: dp
  Button button_7 (.out(Start));
  Hex_Digit_Display hex_digit_display_3 (.value(cifraS3));  // open: dp
  Hex_Digit_Display hex_digit_display_4 (.value(cifraS2));  // open: dp
  LED led_2 (.in(N2));
  Hex_Digit_Display hex_digit_display_5 (.value(cifra2Ins));  // open: dp
  Button button_8 (.out(_1));
  Button button_9 (.out(_2));
  Button button_10 (.out(_5));
  Button button_11 (.out(_4));
  Button button_12 (.out(_7));
  Button button_13 (.out(_8));
  Button button_14 (.out(_0));
  Button button_15 (.out(_1946));
  Button button_16 (.out(_1944));
  Button button_17 (.out(Falso));
  Button button_18 (.out(REAL_MADRID));
  Button button_19 (.out(BOCA_JUNIORS));
  Button button_20 (.out(Falso2));
  Hex_Digit_Display hex_digit_display_6 (.value(cifraS4));  // open: dp
  LED led_3 (.in(N3));
  Hex_Digit_Display hex_digit_display_7 (.value(cifra3Ins));  // open: dp
  Hex_Digit_Display hex_digit_display_8 (.value(cifra4Ins));  // open: dp
  Button button_21 (.out(_3));
  Button button_22 (.out(_6));
  Button button_23 (.out(_9));
  LED led_4 (.in(N4));
  Button button_24 (.out(ResetPin));
  DotMatrix #(.inputtype("row"), .matrixcols(32), .matrixrows(15)) dotmatrix_1 (
    .row0(missioncomplete_1_out_2), .row1(missioncomplete_1_out_3), .row2(missioncomplete_1_out_4),
    .row3(missioncomplete_1_out_5), .row4(missioncomplete_1_out_6), .row5(missioncomplete_1_out_7),
    .row6(missioncomplete_1_out_8), .row7(missioncomplete_1_out_9), .row8(missioncomplete_1_out_10),
    .row9(missioncomplete_1_out_11), .row10(missioncomplete_1_out_12), .row11(missioncomplete_1_out_13),
    .row12(missioncomplete_1_out_14), .row13(missioncomplete_1_out_15), .row14(missioncomplete_1_out_16));
  missionComplete missioncomplete_1 (
    .in_1(status), .out_2(missioncomplete_1_out_2), .out_3(missioncomplete_1_out_3),
    .out_4(missioncomplete_1_out_4), .out_5(missioncomplete_1_out_5), .out_6(missioncomplete_1_out_6),
    .out_7(missioncomplete_1_out_7), .out_8(missioncomplete_1_out_8), .out_9(missioncomplete_1_out_9),
    .out_10(missioncomplete_1_out_10), .out_11(missioncomplete_1_out_11), .out_12(missioncomplete_1_out_12),
    .out_13(missioncomplete_1_out_13), .out_14(missioncomplete_1_out_14), .out_15(missioncomplete_1_out_15),
    .out_16(missioncomplete_1_out_16));
  statusCaveau statuscaveau_1 (
    .Status(status), .out_2(statuscaveau_1_out_2), .out_3(statuscaveau_1_out_3),
    .out_4(statuscaveau_1_out_4), .out_5(statuscaveau_1_out_5), .out_6(statuscaveau_1_out_6),
    .out_7(statuscaveau_1_out_7), .out_8(statuscaveau_1_out_8), .out_9(statuscaveau_1_out_9),
    .out_10(statuscaveau_1_out_10), .out_11(statuscaveau_1_out_11), .out_12(statuscaveau_1_out_12),
    .out_13(statuscaveau_1_out_13), .out_14(statuscaveau_1_out_14), .out_15(statuscaveau_1_out_15),
    .out_16(statuscaveau_1_out_16), .out_17(statuscaveau_1_out_17), .out_18(statuscaveau_1_out_18),
    .out_19(statuscaveau_1_out_19), .out_20(statuscaveau_1_out_20), .out_21(statuscaveau_1_out_21));
  DotMatrix #(.inputtype("row"), .matrixcols(19), .matrixrows(20)) dotmatrix_2 (
    .row0(statuscaveau_1_out_2), .row1(statuscaveau_1_out_3), .row2(statuscaveau_1_out_4),
    .row3(statuscaveau_1_out_5), .row4(statuscaveau_1_out_6), .row5(statuscaveau_1_out_7),
    .row6(statuscaveau_1_out_8), .row7(statuscaveau_1_out_9), .row8(statuscaveau_1_out_10),
    .row9(statuscaveau_1_out_11), .row10(statuscaveau_1_out_12), .row11(statuscaveau_1_out_13),
    .row12(statuscaveau_1_out_14), .row13(statuscaveau_1_out_15), .row14(statuscaveau_1_out_16),
    .row15(statuscaveau_1_out_17), .row16(statuscaveau_1_out_18), .row17(statuscaveau_1_out_19),
    .row18(statuscaveau_1_out_20), .row19(statuscaveau_1_out_21));
  Hex_Digit_Display hex_digit_display_9 (.value(min2));  // open: dp
  Hex_Digit_Display hex_digit_display_10 (.value(min1));  // open: dp
  Hex_Digit_Display hex_digit_display_11 (.value(sec1));  // open: dp
  Hex_Digit_Display hex_digit_display_12 (.value(sec2));  // open: dp
  passCode passcode_1 (.genPass(Start), .out_2(cifra1), .out_3(cifra2), .out_4(cifra3), .out_5(cifra4));
  Multiplexer #(.width(4)) multiplexer_1 (.in1(cifra3), .out(cifraS1), .sel(ris1));  // open: in0, en
  Multiplexer #(.width(4)) multiplexer_2 (.in1(cifra1), .out(cifraS3), .sel(ris2));  // open: in0, en
  or or_1 (or_1_out, _1944, _1945, _1947);
  Priority_Encoder #(.select(1)) priority_encoder_1 (
    .in0(Vero), .in1(Falso), .out(priority_encoder_1_out), .gs(priority_encoder_1_gs));  // open: en_out, en_in
  Hex_Digit_Display hex_digit_display_13 (.value(cifra1));  // open: dp
  Hex_Digit_Display hex_digit_display_14 (.value(cifra2));  // open: dp
  Priority_Encoder #(.select(1)) priority_encoder_2 (
    .in0(or_1_out), .in1(_1946), .out(priority_encoder_2_out), .gs(priority_encoder_2_gs));  // open: en_out, en_in
  Shift_Register #(.length(1)) shift_register_1 (
    .shift(1'b1), .in(priority_encoder_1_out), .clk(priority_encoder_1_gs), .clr(in_1), .q0(ris3));  // open: out, load, d0
  Priority_Encoder #(.select(4)) priority_encoder_3 (
    .in0(_0), .in1(_1), .in2(_2), .in3(_3), .in4(_4), .in5(_5), .in6(_6), .in7(_7), .in8(_8), .in9(_9),
    .out(priority_encoder_3_out), .gs(priority_encoder_3_gs));  // open: in10, in11, in12, in13, in14, in15, en_out, en_in
  Clock clock_1 (.out(clock_1_out));
  J_K_Flip_Flop j_k_ff_1 (.J(1'b1), .clk(Start), .K(1'b1), .Qn(j_k_ff_1_qn), .reset(in_1));  // open: Q, preset, en
  Hex_Digit_Display hex_digit_display_15 (.value(cifra3));  // open: dp
  Multiplexer #(.width(4)) multiplexer_3 (.in1(cifra4), .out(cifraS2), .sel(ris3));  // open: in0, en
  Multiplexer #(.width(4)) multiplexer_4 (.in1(cifra2), .out(cifraS4), .sel(ris4));  // open: in0, en
  Shift_Register #(.length(1)) shift_register_2 (
    .shift(1'b1), .in(priority_encoder_2_out), .clk(priority_encoder_2_gs), .clr(in_1), .q0(ris1));  // open: out, load, d0
  Shift_Register #(.width(4), .length(4)) shift_register_3 (
    .shift(1'b1), .in(priority_encoder_3_out), .clk(priority_encoder_3_gs), .clr(or_2_out), .q0(cifra4Ins),
    .q1(cifra3Ins), .q2(cifra2Ins), .q3(cifra1Ins));  // open: out, load, d0, d1, d2, d3
  or or_2 (or_2_out, ResetPin, in_1);
  Comparator #(.width(16), .mode("unsigned")) comparator_1 (
    .a({cifra1Ins, cifra2Ins, cifra3Ins, cifra4Ins}), .b({cifra1, cifra2, cifra3, cifra4}), .eq(status));  // open: gt, lt
  nor nor_1 (nor_1_out, clock_1_out, status, j_k_ff_1_qn);
  near near_1 (.A(cifra1), .B(cifra1Ins), .B_2(cifra1Ins), .A_2(cifra1), .out_5(N1));
  near near_2 (.A(cifra2), .B(cifra2Ins), .B_2(cifra2Ins), .A_2(cifra2), .out_5(N2));
  Hex_Digit_Display hex_digit_display_16 (.value(cifra4));  // open: dp
  or or_3 (or_3_out, stop10_1_output, in_1);
  count4Bit count4bit_1 (.Input(nor_1_out), .Clear(or_3_out), .out_3(sec2));
  stop10 stop10_1 (.Input(sec2), .Output(stop10_1_output));
  or or_4 (or_4_out, stop6_1_output, in_1);
  or or_5 (or_5_out, BOCA_JUNIORS, AL_AHLY, MILAN);
  Priority_Encoder #(.select(1)) priority_encoder_4 (
    .in0(Falso2), .in1(Vero2), .out(priority_encoder_4_out), .gs(priority_encoder_4_gs));  // open: en_out, en_in
  count4Bit count4bit_2 (.Input(stop10_1_output), .Clear(or_4_out), .out_3(sec1));
  Priority_Encoder #(.select(1)) priority_encoder_5 (
    .in0(or_5_out), .in1(REAL_MADRID), .out(priority_encoder_5_out), .gs(priority_encoder_5_gs));  // open: en_out, en_in
  Shift_Register #(.length(1)) shift_register_4 (
    .shift(1'b1), .in(priority_encoder_4_out), .clk(priority_encoder_4_gs), .clr(in_1), .q0(ris4));  // open: out, load, d0
  stop6 stop6_1 (.Input(sec1), .Output(stop6_1_output));
  or or_6 (or_6_out, stop10_2_output, in_1);
  near near_3 (.A(cifra3), .B(cifra3Ins), .B_2(cifra3Ins), .A_2(cifra3), .out_5(N3));
  near near_4 (.A(cifra4), .B(cifra4Ins), .B_2(cifra4Ins), .A_2(cifra4), .out_5(N4));
  Shift_Register #(.length(1)) shift_register_5 (
    .shift(1'b1), .in(priority_encoder_5_out), .clk(priority_encoder_5_gs), .clr(in_1), .q0(ris2));  // open: out, load, d0
  count4Bit count4bit_3 (.Input(stop6_1_output), .Clear(or_6_out), .out_3(min2));
  stop10 stop10_2 (.Input(min2), .Output(stop10_2_output));
  count4Bit count4bit_4 (.Input(stop10_2_output), .Clear(or_7_out), .out_3(min1));
  stop6 stop6_2 (.Input(min1), .Output(stop6_2_output));
  or or_7 (or_7_out, stop6_2_output, in_1);

  // Other names for the same wires on the sheet: Reset = in_1

  // Notes on the sheet:
  //   Istruzioni per giocare:
  //   Progetto a cura di Eldemerdash Ramy 
  //   2 => Il nilo è il fiume più lungo al mondo?
  //   3 => Quale squadra è la più titolata nel mondo?
  //   4 => Il numero 83 è un numero primo?
  //   CIFRE PRESENTI NEL CODICE SEGRETO
  //   CODICE INSERITO
  //   1. Impostare il clock a 2Hz
  //   4. Led = verde -> sei vicino
  //   1 => In quale anno è stata fondata la Repubblica Italiana?
  //   2. Quando sei pronto premi il pulsante Start
  //   3. Rispondendo ai quiz presenti in modo corretto
  //   sbloccherai una cifra del codice segreto
  //   Preparati ad aprire il caveau
  //   🢛🢛🢛🢛🢛🢛
  //   OPEN THE CAVEAU
  //   TEMPO
  //   ■
  //   ■
  //   Gen. secret code
  //   Gestione risposte quiz
  //   Gestione codice inserito
  //   Gestione cronometro
  //   Gestione near
endmodule

module statusCaveau (
  input  Status,
  output [18:0] out_2,
  output [18:0] out_3,
  output [18:0] out_4,
  output [18:0] out_5,
  output [18:0] out_6,
  output [18:0] out_7,
  output [18:0] out_8,
  output [18:0] out_9,
  output [18:0] out_10,
  output [18:0] out_11,
  output [18:0] out_12,
  output [18:0] out_13,
  output [18:0] out_14,
  output [18:0] out_15,
  output [18:0] out_16,
  output [18:0] out_17,
  output [18:0] out_18,
  output [18:0] out_19,
  output [18:0] out_20,
  output [18:0] out_21
);

  Multiplexer #(.width(19)) multiplexer_1 (.in0({19{1'b0}}), .in1({19{1'b0}}), .out(out_2), .sel(Status));  // open: en
  Multiplexer #(.width(19)) multiplexer_2 (.in0({19{1'b0}}), .in1(19'hfff8), .out(out_3), .sel(Status));  // open: en
  Multiplexer #(.width(19)) multiplexer_3 (.in0({19{1'b0}}), .in1({19{1'b0}}), .out(out_4), .sel(Status));  // open: en
  Multiplexer #(.width(19)) multiplexer_4 (.in0({19{1'b0}}), .in1(19'hfff8), .out(out_5), .sel(Status));  // open: en
  Multiplexer #(.width(19)) multiplexer_5 (.in0(19'h700), .in1(19'hfff8), .out(out_6), .sel(Status));  // open: en
  Multiplexer #(.width(19)) multiplexer_6 (.in0(19'h1fc0), .in1(19'h8008), .out(out_7), .sel(Status));  // open: en
  Multiplexer #(.width(19)) multiplexer_7 (.in0(19'h3fe0), .in1(19'hfdf8), .out(out_8), .sel(Status));  // open: en
  Multiplexer #(.width(19)) multiplexer_8 (.in0(19'h78f0), .in1(19'hfdf8), .out(out_9), .sel(Status));  // open: en
  Multiplexer #(.width(19)) multiplexer_9 (.in0(19'hfdf8), .in1(19'h8008), .out(out_10), .sel(Status));  // open: en
  Multiplexer #(.width(19)) multiplexer_10 (.in0(19'he8b8), .in1(19'hfdf8), .out(out_11), .sel(Status));  // open: en
  Multiplexer #(.width(19)) multiplexer_11 (.in0(19'he038), .in1(19'hfdf8), .out(out_12), .sel(Status));  // open: en
  Multiplexer #(.width(19)) multiplexer_12 (.in0(19'he8b8), .in1(19'h8008), .out(out_13), .sel(Status));  // open: en
  Multiplexer #(.width(19)) multiplexer_13 (.in0(19'hfdf8), .in1(19'hfdf8), .out(out_14), .sel(Status));  // open: en
  Multiplexer #(.width(19)) multiplexer_14 (.in0(19'h78f0), .in1(19'hfdf8), .out(out_15), .sel(Status));  // open: en
  Multiplexer #(.width(19)) multiplexer_15 (.in0(19'h3fe0), .in1(19'h8008), .out(out_16), .sel(Status));  // open: en
  Multiplexer #(.width(19)) multiplexer_16 (.in0(19'h1fc0), .in1(19'hfff8), .out(out_17), .sel(Status));  // open: en
  Multiplexer #(.width(19)) multiplexer_17 (.in0(19'h500), .in1(19'hfff8), .out(out_18), .sel(Status));  // open: en
  Multiplexer #(.width(19)) multiplexer_18 (
    .in0({19{1'b0}}), .in1({19{1'b0}}), .out(out_19), .sel(Status));  // open: en
  Multiplexer #(.width(19)) multiplexer_19 (.in0({19{1'b0}}), .in1(19'hfff8), .out(out_20), .sel(Status));  // open: en
  Multiplexer #(.width(19)) multiplexer_20 (
    .in0({19{1'b0}}), .in1({19{1'b0}}), .out(out_21), .sel(Status));  // open: en

  // Notes on the sheet:
  //   0 => Close
  //   1 => Open
endmodule

module passCode (
  input  genPass,
  output [3:0] out_2,
  output [3:0] out_3,
  output [3:0] out_4,
  output [3:0] out_5
);

  wire [2:0] random_1_out, random_2_out, random_3_out, random_4_out;

  Random #(.width(3), .seed(2)) random_1 (.clk(genPass), .out(random_1_out));  // open: next, clr
  Random #(.width(3), .seed(5)) random_2 (.clk(genPass), .out(random_2_out));  // open: next, clr
  Random #(.width(3), .seed(8)) random_3 (.clk(genPass), .out(random_3_out));  // open: next, clr
  Random #(.width(3), .seed(1)) random_4 (.clk(genPass), .out(random_4_out));  // open: next, clr
  assign out_2 = {{1{1'b0}}, random_1_out};  // Bit_Extender bit_extender_1
  assign out_3 = {{1{1'b0}}, random_2_out};  // Bit_Extender bit_extender_2
  assign out_4 = {{1{1'b0}}, random_3_out};  // Bit_Extender bit_extender_3
  assign out_5 = {{1{1'b0}}, random_4_out};  // Bit_Extender bit_extender_4
endmodule

module missionComplete (
  input  in_1,
  output [31:0] out_2,
  output [31:0] out_3,
  output [31:0] out_4,
  output [31:0] out_5,
  output [31:0] out_6,
  output [31:0] out_7,
  output [31:0] out_8,
  output [31:0] out_9,
  output [31:0] out_10,
  output [31:0] out_11,
  output [31:0] out_12,
  output [31:0] out_13,
  output [31:0] out_14,
  output [31:0] out_15,
  output [31:0] out_16
);

  Multiplexer #(.width(32)) multiplexer_1 (.in0({32{1'b0}}), .in1(32'hc6bba661), .out(out_2), .sel(in_1));  // open: en
  Multiplexer #(.width(32)) multiplexer_2 (.in0({32{1'b0}}), .in1(32'haaaaa951), .out(out_3), .sel(in_1));  // open: en
  Multiplexer #(.width(32)) multiplexer_3 (.in0({32{1'b0}}), .in1(32'haaaaa951), .out(out_4), .sel(in_1));  // open: en
  Multiplexer #(.width(32)) multiplexer_4 (.in0({32{1'b0}}), .in1(32'h92a22949), .out(out_5), .sel(in_1));  // open: en
  Multiplexer #(.width(32)) multiplexer_5 (.in0({32{1'b0}}), .in1(32'h82bba949), .out(out_6), .sel(in_1));  // open: en
  Multiplexer #(.width(32)) multiplexer_6 (.in0({32{1'b0}}), .in1(32'h8288a945), .out(out_7), .sel(in_1));  // open: en
  Multiplexer #(.width(32)) multiplexer_7 (.in0({32{1'b0}}), .in1(32'h82aaa945), .out(out_8), .sel(in_1));  // open: en
  Multiplexer #(.width(32)) multiplexer_8 (.in0({32{1'b0}}), .in1(32'h82aaa943), .out(out_9), .sel(in_1));  // open: en
  Multiplexer #(.width(32)) multiplexer_9 (.in0({32{1'b0}}), .in1(32'h82bba641), .out(out_10), .sel(in_1));  // open: en
  Multiplexer #(.width(32)) multiplexer_10 (.in0({32{1'b0}}), .in1({32{1'b0}}), .out(out_11), .sel(in_1));  // open: en
  Multiplexer #(.width(32)) multiplexer_11 (
    .in0({32{1'b0}}), .in1(32'h139ecbc2), .out(out_12), .sel(in_1));  // open: en
  Multiplexer #(.width(32)) multiplexer_12 (
    .in0({32{1'b0}}), .in1(32'h2252aa04), .out(out_13), .sel(in_1));  // open: en
  Multiplexer #(.width(32)) multiplexer_13 (
    .in0({32{1'b0}}), .in1(32'h7252ab8e), .out(out_14), .sel(in_1));  // open: en
  Multiplexer #(.width(32)) multiplexer_14 (
    .in0({32{1'b0}}), .in1(32'h22529a04), .out(out_15), .sel(in_1));  // open: en
  Multiplexer #(.width(32)) multiplexer_15 (
    .in0({32{1'b0}}), .in1(32'h439e8bc8), .out(out_16), .sel(in_1));  // open: en

  // Notes on the sheet:
  //   1 => Mission Complete
endmodule

module _4BitSubtractor (
  input  [3:0] in_1,
  input  [3:0] in_2,
  output [3:0] out_3,
  output Negative
);

  wire full_substractor_1_rest, full_substractor_2_rest, full_substractor_3_rest;

  full_substractor full_substractor_1 (
    .A(in_1[0]), .B(in_2[0]), .Pre_IN(1'b0), .Sub(out_3[0]), .Rest(full_substractor_1_rest));
  full_substractor full_substractor_2 (
    .A(in_1[1]), .B(in_2[1]), .Pre_IN(full_substractor_1_rest), .Sub(out_3[1]), .Rest(full_substractor_2_rest));
  full_substractor full_substractor_3 (
    .A(in_1[2]), .B(in_2[2]), .Pre_IN(full_substractor_2_rest), .Sub(out_3[2]), .Rest(full_substractor_3_rest));
  full_substractor full_substractor_4 (
    .A(in_1[3]), .B(in_2[3]), .Pre_IN(full_substractor_3_rest), .Sub(out_3[3]), .Rest(Negative));
  Hex_Digit_Display hex_digit_display_1 (.value(out_3));  // open: dp

  // Other names for the same wires on the sheet: A0 = in_1[0]; A1 = in_1[1]; A2 = in_1[2]; A3 = in_1[3]; B0 = in_2[0];
  //   B1 = in_2[1]; B2 = in_2[2]; B3 = in_2[3]
endmodule

module full_substractor (
  input  A,
  input  B,
  input  Pre_IN,
  output Sub,
  output Rest
);

  wire and_1_out, and_2_out, and_3_out, not_1_out, or_1_out, xor_1_out;

  not not_1 (not_1_out, A);
  and and_1 (and_1_out, not_1_out, B);
  and and_2 (and_2_out, not_1_out, Pre_IN);
  xor xor_1 (xor_1_out, A, B);
  or or_1 (or_1_out, and_1_out, and_2_out);
  and and_3 (and_3_out, B, Pre_IN);
  xor xor_2 (Sub, xor_1_out, Pre_IN);
  or or_2 (Rest, or_1_out, and_3_out);
endmodule

module near (
  input  [3:0] A,
  input  [3:0] B,
  input  [3:0] B_2,
  input  [3:0] A_2,
  output out_5
);

  wire comparator_1_eq, comparator_1_lt, negative;
  wire [3:0] near, near_plus, ris;

  _4BitSubtractor u_4bitsubtractor_1 (.in_1(A), .in_2(B_2), .out_3(near), .Negative(negative));
  Multiplexer #(.width(4)) multiplexer_1 (.in0(near), .in1(near_plus), .out(ris), .sel(negative));  // open: en
  Comparator #(.width(4), .mode("unsigned")) comparator_1 (
    .a(ris), .b(4'b0011), .eq(comparator_1_eq), .lt(comparator_1_lt));  // open: gt
  or or_1 (out_5, comparator_1_eq, comparator_1_lt);
  LED led_1 (.in(out_5));
  _4BitSubtractor u_4bitsubtractor_2 (.in_1(B), .in_2(A_2), .out_3(near_plus));  // open: Negative

  // Notes on the sheet:
  //   sottrazione > 0
  //   sottrazione < 0
endmodule
